// Logisim project s-mips.circ as structural Verilog: 23 circuits, main circuit S-MIPS Board
module S_MIPS_Board (
  input  DESHABILITAR_DISPATCHER,
  output halt
);

  wire button_1_out, CLK, CS, d_ff_1_q, LCLR, LoadRAM, LoadRAMOn, LW, R_R_W, R_W, ram_dispatcher_1_finished,
       RCS, Reset_out, RST, TTY_EN;
  wire [2:0] KDB;
  wire [3:0] LMask, Mask, ram_1_read_time, ram_1_write_time, RMask;
  wire [6:0] KDB_DATA, TTY_DATA;
  wire [15:0] Addr, LAddr, RAddr;
  wire [31:0] I0, I1, I2, I3, LData, ram_1_data_out_0, ram_1_data_out_1, ram_1_data_out_2, ram_1_data_out_3,
       RI0, RI1, RI2, RI3;

  TTY #(.rows(25), .cols(80)) tty_1 (.data(TTY_DATA), .clk(CLK), .we(TTY_EN), .clr(RST));
  not not_1 (LoadRAMOn, ram_dispatcher_1_finished);
  RAM_Dispatcher ram_dispatcher_1 (
    .WriteTime(ram_1_write_time), .Clock(CLK), .Data(LData), .Address(LAddr), .Mask(LMask),
    .Finished(ram_dispatcher_1_finished), .Write(LW), .CLR(LCLR));
  Keyboard #(.buflen(64)) keyboard_1 (.clk(CLK), .re(KDB[0]), .avail(KDB[2]), .data(KDB_DATA));  // open: clr
  RAM ram_1 (
    .Address(RAddr), .Data_Out_0(ram_1_data_out_0), .Data_Out_1(ram_1_data_out_1),
    .Data_Out_2(ram_1_data_out_2), .Data_Out_3(ram_1_data_out_3), .Data_In_0(RI0), .Data_In_1(RI1),
    .Data_In_2(RI2), .Data_In_3(RI3), .Mask(RMask), .nRead_Write(R_R_W), .Chip_Select(RCS),
    .Read_Time(ram_1_read_time), .Reset(button_1_out), .Write_Time(ram_1_write_time));
  Button button_1 (.out(button_1_out));
  D_Flip_Flop d_ff_1 (.clk(CLK), .D(1'b1), .Q(d_ff_1_q), .reset(Reset_out));  // open: Qn, preset, en
  Button Reset (.out(Reset_out));
  S_MIPS s_mips_1 (
    .Kbd_Enable(KDB[0]), .Address(Addr), .Kbd_Clear(KDB[1]), .Kbd_Available(KDB[2]), .RAM_In_0(I0),
    .Kbd_ASCII_Data(KDB_DATA), .RAM_In_1(I1), .TTY_Enable(TTY_EN), .RAM_In_2(I2), .RAM_In_3(I3),
    .TTY_ASCII_Data(TTY_DATA), .Reset(RST), .RAM_Out_0(ram_1_data_out_0), .Clock(CLK),
    .RAM_Out_1(ram_1_data_out_1), .Stop(halt), .RAM_Out_2(ram_1_data_out_2), .RAM_Out_3(ram_1_data_out_3),
    .Mask(Mask), .Read_Time(ram_1_read_time), .Write_Time(ram_1_write_time), .nRead_Write(R_W),
    .Chip_Select(CS));
  D_Flip_Flop d_ff_2 (.clk(CLK), .D(d_ff_1_q), .Qn(LCLR), .reset(Reset_out));  // open: Q, preset, en
  or or_1 (RST, LCLR, LoadRAM);
  Clock clock_1 (.out(CLK));
  Multiplexer #(.width(32), .enable("false")) multiplexer_1 (.in0(I0), .in1(LData), .out(RI0), .sel(LoadRAM));
  Multiplexer #(.width(32), .enable("false")) multiplexer_2 (.in0(I1), .in1(LData), .out(RI1), .sel(LoadRAM));
  Multiplexer #(.width(32), .enable("false")) multiplexer_3 (.in0(I2), .in1(LData), .out(RI2), .sel(LoadRAM));
  Multiplexer #(.width(32), .enable("false")) multiplexer_4 (.in0(I3), .in1(LData), .out(RI3), .sel(LoadRAM));
  and and_1 (LoadRAM, ~DESHABILITAR_DISPATCHER, LoadRAMOn);  // AND_Gate
  Multiplexer #(.width(16), .enable("false")) multiplexer_5 (.in0(Addr), .in1(LAddr), .out(RAddr), .sel(LoadRAM));
  Multiplexer #(.width(4), .enable("false")) multiplexer_6 (.in0(Mask), .in1(LMask), .out(RMask), .sel(LoadRAM));
  Multiplexer #(.enable("false")) multiplexer_7 (.in0(CS), .in1(LW), .out(RCS), .sel(LoadRAM));
  Multiplexer #(.enable("false")) multiplexer_8 (.in0(R_W), .in1(LW), .out(R_R_W), .sel(LoadRAM));

  // Notes on the sheet:
  //   NO MODIFICAR
  //   Keyboard
endmodule

module RAM (
  input  [15:0] Address,
  input  [31:0] Data_In_0,
  input  [31:0] Data_In_1,
  input  [31:0] Data_In_2,
  input  [31:0] Data_In_3,
  input  [3:0] Mask,
  input  nRead_Write,
  input  Chip_Select,
  input  Reset,
  output [31:0] Data_Out_0,
  output [31:0] Data_Out_1,
  output [31:0] Data_Out_2,
  output [31:0] Data_Out_3,
  output [3:0] Read_Time,
  output [3:0] Write_Time
);

  wire and_2_out, and_3_out, and_4_out, and_5_out, and_6_out, and_7_out, and_8_out, and_9_out, Changed, CLK,
       comparator_2_eq, comparator_3_eq, comparator_4_eq, comparator_5_eq, comparator_6_eq, Count,
       demultiplexer_3_out0, Idle, Idle_q, Load, Load0, Load1, nand_1_out, or_1_out, or_2_out, or_3_out,
       or_4_out, or_5_out, or_6_out, or_7_out, or_8_out, or_9_out, or_10_out, Proc_q, Update_Mem, Zero_Time;
  wire [3:0] counter_1_q, multiplexer_1_out, subtractor_1_out;
  wire [31:0] register_1_q, register_2_q, register_3_q, register_4_q, register_5_q;

  // Probe on 4'b0011
  // Probe on 4'b0010
  Multiplexer #(.width(4), .enable("false")) multiplexer_1 (
    .in0(4'b0011), .in1(4'b0010), .out(multiplexer_1_out), .sel(nRead_Write));
  or or_1 (or_1_out, Idle, Update_Mem);
  or or_2 (or_2_out, ~Chip_Select, Reset);  // OR_Gate
  Subtractor #(.width(4)) subtractor_1 (.a(multiplexer_1_out), .b(4'b0010), .out(subtractor_1_out));  // open: bin, bout
  D_Flip_Flop u_Idle (.clk(CLK), .D(or_1_out), .Q(Idle_q), .preset(or_2_out));  // open: Qn, en, reset
  Demultiplexer #(.enable("false")) demultiplexer_1 (.out0(Idle), .out1(Load0), .in(Idle_q), .sel(Changed));
  // Probe on counter_1_q
  Counter #(.width(4), .max('hf)) counter_1 (
    .load(Load), .D(subtractor_1_out), .count(Count), .Q(counter_1_q), .clk(CLK), .clr(or_3_out));  // open: carry
  or or_3 (or_3_out, ~Chip_Select, Reset);  // OR_Gate
  Comparator #(.width(4), .mode("unsigned")) comparator_1 (
    .a(4'b0000), .b(counter_1_q), .eq(Zero_Time));  // open: gt, lt
  or or_4 (or_4_out, Count, Load0, Load1);
  Register #(.width(32)) register_1 (.D(Data_In_0), .en(Chip_Select), .Q(register_1_q), .clk(CLK), .clr(or_5_out));
  or or_5 (or_5_out, ~Chip_Select, Reset);  // OR_Gate
  Register #(.width(32)) register_2 (.D(Data_In_1), .en(Chip_Select), .Q(register_2_q), .clk(CLK), .clr(or_6_out));
  or or_6 (or_6_out, ~Chip_Select, Reset);  // OR_Gate
  Register #(.width(32)) register_3 (.D(Data_In_2), .en(Chip_Select), .Q(register_3_q), .clk(CLK), .clr(or_7_out));
  or or_7 (or_7_out, ~Chip_Select, Reset);  // OR_Gate
  Register #(.width(32)) register_4 (.D(Data_In_3), .en(Chip_Select), .Q(register_4_q), .clk(CLK), .clr(or_8_out));
  or or_8 (or_8_out, ~Chip_Select, Reset);  // OR_Gate
  Register #(.width(32)) register_5 (
    .D({{11{1'b1}}, nRead_Write, Mask, Address}), .en(Chip_Select), .Q(register_5_q), .clk(CLK),
    .clr(or_9_out));
  or or_9 (or_9_out, ~Chip_Select, Reset);  // OR_Gate
  D_Flip_Flop Proc (.clk(CLK), .D(or_4_out), .Q(Proc_q), .reset(or_10_out));  // open: Qn, preset, en
  or or_10 (or_10_out, ~Chip_Select, Reset);  // OR_Gate
  Demultiplexer #(.enable("false")) demultiplexer_2 (
    .out0(Count), .out1(Update_Mem), .in(demultiplexer_3_out0), .sel(Zero_Time));
  Demultiplexer #(.enable("false")) demultiplexer_3 (
    .out0(demultiplexer_3_out0), .out1(Load1), .in(Proc_q), .sel(Changed));
  Clock clock_1 (.out(CLK));
  Comparator #(.width(32)) comparator_2 (.a(register_1_q), .b(Data_In_0), .eq(comparator_2_eq));  // open: gt, lt
  Comparator #(.width(32)) comparator_3 (.a(register_2_q), .b(Data_In_1), .eq(comparator_3_eq));  // open: gt, lt
  Comparator #(.width(32)) comparator_4 (.a(register_3_q), .b(Data_In_2), .eq(comparator_4_eq));  // open: gt, lt
  Comparator #(.width(32)) comparator_5 (.a(register_4_q), .b(Data_In_3), .eq(comparator_5_eq));  // open: gt, lt
  Comparator #(.width(32)) comparator_6 (
    .a(register_5_q), .b({{11{1'b1}}, nRead_Write, Mask, Address}), .eq(comparator_6_eq));  // open: gt, lt
  nand nand_1 (nand_1_out, comparator_6_eq, comparator_2_eq, comparator_3_eq, comparator_4_eq, comparator_5_eq);
  and and_1 (Changed, nand_1_out, Chip_Select);
  or or_11 (Load, Count, Load1, Load0);
  and and_2 (and_2_out, Mask[0], Update_Mem, nRead_Write);
  and and_3 (and_3_out, Mask[1], Update_Mem, nRead_Write);
  and and_4 (and_4_out, Mask[2], Update_Mem, nRead_Write);
  and and_5 (and_5_out, Mask[3], Update_Mem, nRead_Write);
  RAM_part #(.addrWidth(16), .dataWidth(32), .bus("separate")) ram_1 (
    .addr(Address), .din(Data_In_0), .data(Data_Out_0), .str(and_2_out), .sel(Chip_Select), .clk(CLK),
    .ld(and_6_out), .clr(Reset));
  and and_6 (and_6_out, ~nRead_Write, Idle);  // AND_Gate
  RAM_part #(.addrWidth(16), .dataWidth(32), .bus("separate")) ram_2 (
    .addr(Address), .din(Data_In_1), .data(Data_Out_1), .str(and_3_out), .sel(Chip_Select), .clk(CLK),
    .ld(and_7_out), .clr(Reset));
  and and_7 (and_7_out, ~nRead_Write, Idle);  // AND_Gate
  RAM_part #(.addrWidth(16), .dataWidth(32), .bus("separate")) ram_3 (
    .addr(Address), .din(Data_In_2), .data(Data_Out_2), .str(and_4_out), .sel(Chip_Select), .clk(CLK),
    .ld(and_8_out), .clr(Reset));
  and and_8 (and_8_out, ~nRead_Write, Idle);  // AND_Gate
  RAM_part #(.addrWidth(16), .dataWidth(32), .bus("separate")) ram_4 (
    .addr(Address), .din(Data_In_3), .data(Data_Out_3), .str(and_5_out), .sel(Chip_Select), .clk(CLK),
    .ld(and_9_out), .clr(Reset));
  and and_9 (and_9_out, ~nRead_Write, Idle);  // AND_Gate

  assign Read_Time = 4'b0011;
  assign Write_Time = 4'b0010;

  // Other names for the same wires on the sheet: M0 = Mask[0]; M1 = Mask[1]; M2 = Mask[2]; M3 = Mask[3];
  //   RW = nRead_Write; CLR = Reset; CS = Chip_Select; Load2 = Count

  // Notes on the sheet:
  //   NO MODIFICAR
  //   excepto quizás los valores RT y WT
  //   BANK0
  //   BANK1
  //   BANK2
  //   BANK3
endmodule

module S_MIPS (
  input  Kbd_Available,
  input  [6:0] Kbd_ASCII_Data,
  input  [31:0] RAM_Out_0,
  input  [31:0] RAM_Out_1,
  input  Reset,
  input  [31:0] RAM_Out_2,
  input  Clock,
  input  [31:0] RAM_Out_3,
  input  [3:0] Read_Time,
  input  [3:0] Write_Time,
  output Kbd_Enable,
  output [15:0] Address,
  output Kbd_Clear,
  output TTY_Enable,
  output [6:0] TTY_ASCII_Data,
  output Stop,
  output [31:0] RAM_In_0,
  output [31:0] RAM_In_1,
  output [31:0] RAM_In_2,
  output [31:0] RAM_In_3,
  output [3:0] Mask,
  output nRead_Write,
  output Chip_Select
);

  wire AluInst, d_ff_2_q, enGI, enPC, enRF, getData, getIsnt, Halt, JmpInst, MemInst, or_1_out, or_2_out,
       ReadyData, ReadyInst, ReadyW, RInst, StackInst, Start, Tty, Write, WriteInst;
  wire [31:0] Adderss, Banck0, Banck0Out, Banck1, Banck1Out, Banck2, Banck2Out, Banck3, Banck3Out, DataIn,
       datapath_1_rout;

  D_Flip_Flop #(.trigger("falling")) d_ff_1 (.clk(Clock), .D(Reset), .Q(Start));  // open: Qn, preset, en, reset
  or or_1 (or_1_out, MemInst, StackInst);
  Multiplexer #(.width(32)) multiplexer_1 (.in0(RAM_Out_0), .in1(RAM_In_0), .out(Banck0), .sel(Write));  // open: en
  Multiplexer #(.width(32)) multiplexer_2 (.in0(RAM_Out_1), .in1(RAM_In_0), .out(Banck1), .sel(Write));  // open: en
  Multiplexer #(.width(32)) multiplexer_3 (.in0(RAM_Out_2), .in1(RAM_In_0), .out(Banck2), .sel(Write));  // open: en
  Multiplexer #(.width(32)) multiplexer_4 (.in0(RAM_Out_3), .in1(RAM_In_0), .out(Banck3), .sel(Write));  // open: en
  Multiplexer #(.select(2), .width(32)) multiplexer_5 (
    .in0(Banck0Out), .in1(Banck1Out), .in2(Banck2Out), .in3(Banck3Out), .out(DataIn), .sel(Adderss[3:2]));  // open: en
  ControlUnit controlunit_1 (
    .in_1(Clock), .in_2(Start), .in_3(ReadyInst), .in_4(AluInst), .in_5(RInst), .in_6(Reset), .in_7(Tty),
    .in_8(ReadyData), .in_9(JmpInst), .in_10(or_1_out), .in_11(WriteInst), .in_12(ReadyW), .out_13(enRF),
    .out_14(enPC), .out_15(Stop), .out_16(getData), .out_18(enGI), .out_21(Write), .out_19(TTY_Enable),
    .out_17(getIsnt), .out_20(Kbd_Enable));
  InteractuarConRam interactuarconram_1 (
    .in_2(Banck0), .in_7(Banck1), .in_11(Banck2), .in_13(Banck3), .in_3(Adderss), .in_12(Read_Time),
    .in_10(Write_Time), .in_1(Clock), .in_6(Reset), .in_5(Write), .in_8(getIsnt), .in_9(getData),
    .in_4(enGI), .out_15(Banck0Out), .out_21(Banck1Out), .out_23(Banck2Out), .out_24(Banck3Out),
    .out_19(Address), .out_22(Mask), .out_16(nRead_Write), .out_14(Chip_Select), .out_17(ReadyInst),
    .out_18(ReadyData), .out_20(ReadyW));
  D_Flip_Flop #(.trigger("falling")) d_ff_2 (
    .clk(Clock), .D(getIsnt), .Q(d_ff_2_q), .en(or_2_out));  // open: Qn, preset, reset
  or or_2 (or_2_out, getIsnt, ReadyInst);
  DataPath datapath_1 (
    .in_3(Clock), .in_5(Reset), .in_6(Kbd_Available), .in_8(d_ff_2_q), .in_4(enRF), .in_7(enPC),
    .in_1(DataIn), .out_13(Halt), .out_15(AluInst), .out_17(RInst), .out_19(JmpInst), .in_2(Kbd_ASCII_Data),
    .out_14(Tty), .out_16(MemInst), .out_18(StackInst), .out_20(WriteInst), .Address(Adderss),
    .TtyData(TTY_ASCII_Data), .ROut(datapath_1_rout), .in_9(enGI));
  InOut inout_1 (.in_1(datapath_1_rout), .Output(RAM_In_0));

  assign Kbd_Clear = Reset;
  assign RAM_In_1 = RAM_In_0;
  assign RAM_In_2 = RAM_In_0;
  assign RAM_In_3 = RAM_In_0;

  // Other names for the same wires on the sheet: CLK = Clock; CS = Chip_Select; KBD_AVAIL = Kbd_Available;
  //   CLR = Reset; KBD_CLR = Reset; KBD_DATA[6:0] = Kbd_ASCII_Data; RAM_A[15:0] = Address; RAM_MASK[3:0] = Mask;
  //   RAM_OUTPUT_0[31:0] = RAM_Out_0; RAM_OUTPUT_1[31:0] = RAM_Out_1; RAM_OUTPUT_2[31:0] = RAM_Out_2;
  //   RAM_OUTPUT_3[31:0] = RAM_Out_3; RAM_INPUT_0[31:0] = RAM_In_0; RAM_INPUT_1[31:0] = RAM_In_0;
  //   RAM_INPUT_2[31:0] = RAM_In_0; RAM_INPUT_3[31:0] = RAM_In_0; ROut[31:0] = RAM_In_0; RW = nRead_Write;
  //   TTY_DATA[6:0] = TTY_ASCII_Data

  // Notes on the sheet:
  //   RAM ADDRESS
  //   DATA FROM RAM
  //   DATA TO RAM
  //   DATA WRITE MASK
  //   RAM TIMING
  //   RAM CONTROL
  //   KEYBOARD
  //   TTY
  //   SEQUENCING
endmodule

module RAM_Dispatcher (
  input  [3:0] WriteTime,
  input  Clock,
  input  CLR,
  output [31:0] Data,
  output [15:0] Address,
  output [3:0] Mask,
  output Finished,
  output Write
);

  wire demultiplexer_2_out1, demultiplexer_3_out1, End, IDLE_q, IncAddr, Load, or_1_out, or_2_out, While_q,
       WriteEnd;
  wire [3:0] counter_1_q;
  wire [31:0] CurrentAddress_q;

  Counter #(.width(32), .max('hffffffff)) CurrentAddress (
    .count(IncAddr), .Q({CurrentAddress_q[31:18], Address, CurrentAddress_q[1:0]}), .clk(Clock), .clr(CLR));  // open: load, D, carry
  or or_1 (or_1_out, IncAddr, demultiplexer_3_out1, Finished);
  D_Flip_Flop IDLE (.clk(Clock), .D(or_1_out), .Q(IDLE_q), .preset(CLR));  // open: Qn, en, reset
  Demultiplexer #(.enable("false")) demultiplexer_1 (.out0(Load), .out1(Finished), .in(IDLE_q), .sel(End));
  D_Flip_Flop While (.clk(Clock), .D(or_2_out), .Q(While_q), .reset(CLR));  // open: Qn, preset, en
  or or_2 (or_2_out, Write, Load);
  RAM_part #(.addrWidth(18), .dataWidth(32)) ram_1 (
    .addr({Address, CurrentAddress_q[1:0]}), .data(Data), .clk(Clock));  // open: sel, ld, clr
  Demultiplexer #(.enable("false")) demultiplexer_2 (
    .out0(Write), .out1(demultiplexer_2_out1), .in(While_q), .sel(WriteEnd));
  Decoder #(.select(2)) decoder_1 (
    .out0(Mask[0]), .out1(Mask[1]), .out2(Mask[2]), .out3(Mask[3]), .sel(CurrentAddress_q[1:0]));  // open: en
  Demultiplexer #(.enable("false")) demultiplexer_3 (
    .out0(IncAddr), .out1(demultiplexer_3_out1), .in(demultiplexer_2_out1), .sel(End));
  Counter #(.width(4), .max('hf)) counter_1 (
    .load(Load), .D(WriteTime), .count(Write), .Q(counter_1_q), .clk(Clock));  // open: carry, clr
  Comparator #(.width(32)) comparator_1 (.a(Data), .b({32{1'b1}}), .eq(End));  // open: gt, lt
  Comparator #(.width(4)) comparator_2 (.a(4'b0000), .b(counter_1_q), .eq(WriteEnd));  // open: gt, lt

  // Other names for the same wires on the sheet: CLK = Clock; Count = Write; WT[3:0] = WriteTime
endmodule

// RF
module RegisterFile (
  input  in_1,
  input  in_2,
  input  [4:0] in_3,
  input  [4:0] in_4,
  input  [4:0] in_5,
  input  in_6,
  input  in_7,
  input  in_8,
  input  in_9,
  input  [31:0] in_10,
  output [31:0] OX,
  output [31:0] OY,
  output [31:0] SP
);

  wire EN_R0, EN_R1, EN_R2, EN_R3, EN_R4, EN_R5, EN_R6, EN_R7, EN_R8, EN_R9, EN_R10, EN_R11, EN_R12, EN_R13,
       EN_R14, EN_R15, EN_R16, EN_R17, EN_R18, EN_R19, EN_R20, EN_R21, EN_R22, EN_R23, EN_R24, EN_R25,
       EN_R26, EN_R27, EN_R28, EN_R29, EN_R30, EN_R31, enR31, or_1_out, or_2_out;
  wire [31:0] adder_1_out, multiplexer_2_out, multiplexer_3_out, Out0, Out1, Out2, Out3, Out4, Out5, Out6,
       Out7, Out8, Out9, Out10, Out11, Out12, Out13, Out14, Out15, Out16, Out17, Out18, Out19, Out20, Out21,
       Out22, Out23, Out24, Out25, Out26, Out27, Out28, Out29, Out30, SP_t, subtractor_1_out;

  Demultiplexer #(.select(5)) demultiplexer_1 (
    .out0(EN_R0), .out1(EN_R1), .out2(EN_R2), .out3(EN_R3), .out4(EN_R4), .out5(EN_R5), .out6(EN_R6),
    .out7(EN_R7), .out8(EN_R8), .out9(EN_R9), .out10(EN_R10), .out11(EN_R11), .out12(EN_R12), .out13(EN_R13),
    .out14(EN_R14), .out15(EN_R15), .out16(EN_R16), .out17(EN_R17), .out18(EN_R18), .out19(EN_R19),
    .out20(EN_R20), .out21(EN_R21), .out22(EN_R22), .out23(EN_R23), .out24(EN_R24), .out25(EN_R25),
    .out26(EN_R26), .out27(EN_R27), .out28(EN_R28), .out29(EN_R29), .out30(EN_R30), .out31(enR31), .in(in_6),
    .sel(in_3));  // open: en
  or or_1 (or_1_out, in_8, in_9);
  and and_1 (EN_R31, or_1_out, in_7);
  Subtractor #(.width(32)) subtractor_1 (.a(SP), .b(32'h4), .out(subtractor_1_out));  // open: bin, bout
  Adder #(.width(32)) adder_1 (.a(32'h4), .b(SP), .out(adder_1_out));  // open: cin, cout
  Multiplexer #(.width(32)) multiplexer_1 (
    .in0(multiplexer_2_out), .in1({32{1'b1}}), .out(SP_t), .sel(in_2));  // open: en
  Multiplexer #(.width(32)) multiplexer_2 (
    .in0(subtractor_1_out), .in1(adder_1_out), .out(multiplexer_2_out), .sel(in_9));  // open: en
  Register #(.width(32)) register_1 (.D({32{1'b0}}), .en(EN_R0), .Q(Out0), .clk(in_1), .clr(in_2));
  Register #(.width(32)) register_2 (.D(in_10), .en(EN_R6), .Q(Out6), .clk(in_1), .clr(in_2));
  Register #(.width(32)) register_3 (.D(in_10), .en(EN_R12), .Q(Out12), .clk(in_1), .clr(in_2));
  Register #(.width(32)) register_4 (.D(in_10), .en(EN_R18), .Q(Out18), .clk(in_1), .clr(in_2));
  Register #(.width(32)) register_5 (.D(in_10), .en(EN_R24), .Q(Out24), .clk(in_1), .clr(in_2));
  Register #(.width(32)) register_6 (.D(in_10), .en(EN_R1), .Q(Out1), .clk(in_1), .clr(in_2));
  Register #(.width(32)) register_7 (.D(in_10), .en(EN_R7), .Q(Out7), .clk(in_1), .clr(in_2));
  Register #(.width(32)) register_8 (.D(in_10), .en(EN_R13), .Q(Out13), .clk(in_1), .clr(in_2));
  Register #(.width(32)) register_9 (.D(in_10), .en(EN_R19), .Q(Out19), .clk(in_1), .clr(in_2));
  Register #(.width(32)) register_10 (.D(in_10), .en(EN_R25), .Q(Out25), .clk(in_1), .clr(in_2));
  Register #(.width(32)) register_11 (.D(in_10), .en(EN_R30), .Q(Out30), .clk(in_1), .clr(in_2));
  Register #(.width(32)) register_12 (.D(in_10), .en(EN_R2), .Q(Out2), .clk(in_1), .clr(in_2));
  Register #(.width(32)) register_13 (.D(in_10), .en(EN_R8), .Q(Out8), .clk(in_1), .clr(in_2));
  Register #(.width(32)) register_14 (.D(in_10), .en(EN_R14), .Q(Out14), .clk(in_1), .clr(in_2));
  Register #(.width(32)) register_15 (.D(in_10), .en(EN_R20), .Q(Out20), .clk(in_1), .clr(in_2));
  Register #(.width(32)) register_16 (.D(in_10), .en(EN_R26), .Q(Out26), .clk(in_1), .clr(in_2));
  Register #(.width(32)) register_17 (.D(in_10), .en(EN_R3), .Q(Out3), .clk(in_1), .clr(in_2));
  Register #(.width(32)) register_18 (.D(in_10), .en(EN_R9), .Q(Out9), .clk(in_1), .clr(in_2));
  Register #(.width(32)) register_19 (.D(in_10), .en(EN_R15), .Q(Out15), .clk(in_1), .clr(in_2));
  Register #(.width(32)) register_20 (.D(in_10), .en(EN_R21), .Q(Out21), .clk(in_1), .clr(in_2));
  Register #(.width(32)) register_21 (.D(in_10), .en(EN_R27), .Q(Out27), .clk(in_1), .clr(in_2));
  Multiplexer #(.width(32)) multiplexer_3 (.in0(SP_t), .in1(in_10), .out(multiplexer_3_out), .sel(enR31));  // open: en
  Register #(.width(32)) register_22 (.D(in_10), .en(EN_R4), .Q(Out4), .clk(in_1), .clr(in_2));
  Register #(.width(32)) register_23 (.D(in_10), .en(EN_R10), .Q(Out10), .clk(in_1), .clr(in_2));
  Register #(.width(32)) register_24 (.D(in_10), .en(EN_R16), .Q(Out16), .clk(in_1), .clr(in_2));
  Register #(.width(32)) register_25 (.D(in_10), .en(EN_R22), .Q(Out22), .clk(in_1), .clr(in_2));
  Register #(.width(32)) register_26 (.D(in_10), .en(EN_R28), .Q(Out28), .clk(in_1), .clr(in_2));
  or or_2 (or_2_out, EN_R31, enR31, in_2);
  Register #(.width(32)) register_27 (.D(in_10), .en(EN_R5), .Q(Out5), .clk(in_1), .clr(in_2));
  Register #(.width(32)) register_28 (.D(in_10), .en(EN_R11), .Q(Out11), .clk(in_1), .clr(in_2));
  Register #(.width(32)) register_29 (.D(in_10), .en(EN_R17), .Q(Out17), .clk(in_1), .clr(in_2));
  Register #(.width(32)) register_30 (.D(in_10), .en(EN_R23), .Q(Out23), .clk(in_1), .clr(in_2));
  Register #(.width(32)) register_31 (.D(in_10), .en(EN_R29), .Q(Out29), .clk(in_1), .clr(in_2));
  Register #(.width(32)) register_32 (.D(multiplexer_3_out), .en(or_2_out), .Q(SP), .clk(in_1));  // open: clr
  Multiplexer #(.select(5), .width(32)) multiplexer_4 (
    .in0(Out0), .in1(Out1), .in2(Out2), .in3(Out3), .in4(Out4), .in5(Out5), .in6(Out6), .in7(Out7),
    .in8(Out8), .in9(Out9), .in10(Out10), .in11(Out11), .in12(Out12), .in13(Out13), .in14(Out14),
    .in15(Out15), .in16(Out16), .in17(Out17), .in18(Out18), .in19(Out19), .in20(Out20), .in21(Out21),
    .in22(Out22), .in23(Out23), .in24(Out24), .in25(Out25), .in26(Out26), .in27(Out27), .in28(Out28),
    .in29(Out29), .in30(Out30), .in31(SP), .out(OX), .sel(in_4));  // open: en
  Multiplexer #(.select(5), .width(32)) multiplexer_5 (
    .in0(Out0), .in1(Out1), .in2(Out2), .in3(Out3), .in4(Out4), .in5(Out5), .in6(Out6), .in7(Out7),
    .in8(Out8), .in9(Out9), .in10(Out10), .in11(Out11), .in12(Out12), .in13(Out13), .in14(Out14),
    .in15(Out15), .in16(Out16), .in17(Out17), .in18(Out18), .in19(Out19), .in20(Out20), .in21(Out21),
    .in22(Out22), .in23(Out23), .in24(Out24), .in25(Out25), .in26(Out26), .in27(Out27), .in28(Out28),
    .in29(Out29), .in30(Out30), .in31(SP), .out(OY), .sel(in_5));  // open: en

  // Other names for the same wires on the sheet: A[31:0] = OX; B[31:0] = OY; Clk = in_1; enPC = in_7;
  //   In[31:0] = in_10; Out31[31:0] = SP; Pop = in_9; Push = in_8; Reset = in_2; RW = in_6; SA[4:0] = in_4;
  //   SB[4:0] = in_5; Select[4:0] = in_3
endmodule

// RF(in)
module ProcessInRF (
  input  in_1,
  input  in_2,
  input  in_3,
  input  [31:0] in_4,
  input  in_5,
  input  in_6,
  input  in_7,
  input  [31:0] in_8,
  input  [31:0] in_9,
  input  [6:0] in_10,
  input  [31:0] in_11,
  input  [31:0] in_12,
  output [31:0] out_13
);

  wire [2:0] Select;
  wire [31:0] Kdb;

  Multiplexer #(.select(3), .width(32)) multiplexer_1 (
    .in0(in_4), .in1(in_9), .in2(in_11), .in3(in_12), .in4(in_8), .in5(Kdb), .out(out_13), .sel(Select));  // open: in6, in7, en
  or or_1 (Select[0], in_1, in_2, in_5, in_6);
  or or_2 (Select[1], in_3, in_5);
  or or_3 (Select[2], in_7, in_6);

  // Other names for the same wires on the sheet: ALU[31:0] = in_4; HI[31:0] = in_11; isKbd = in_6; isRnd = in_7;
  //   Kbd[6:0] = in_10; LO[31:0] = in_12; Lw = in_1; MemX[31:0] = in_9; Mfhi = in_3; Mflo = in_5; OUT[31:0] = out_13;
  //   Pop = in_2; RND[31:0] = in_8
endmodule

module ALU (
  input  [31:0] X,
  input  [31:0] Y,
  input  [3:0] in_3,
  input  in_4,
  input  in_5,
  output [31:0] OUT,
  output [31:0] OH,
  output [31:0] OL
);

  wire and_3_out, comp_1_comp, Enable, mult;
  wire [31:0] ADD, AND, Div, DivRem, MultH, multiplexer_1_out, multiplexer_2_out, MultL, NOR, OR, SLT, SUB,
       XOR;

  Adder #(.width(32)) adder_1 (.a(X), .b(Y), .out(ADD));  // open: cin, cout
  Subtractor #(.width(32)) subtractor_1 (.a(X), .b(Y), .out(SUB));  // open: bin, bout
  assign AND = X & Y;  // AND_Gate and_1, 32 bits wide
  assign OR = X | Y;  // OR_Gate or_1, 32 bits wide
  assign NOR = ~(X | Y);  // NOR_Gate nor_1, 32 bits wide
  assign XOR = X ^ Y;  // XOR_Gate xor_1, 32 bits wide
  Comp comp_1 (.in_1(X), .in_2(Y), .in_3(in_5), .Comp(comp_1_comp));
  assign SLT = {{31{1'b0}}, comp_1_comp};  // Bit_Extender bit_extender_1
  Multi multi_1 (.in_1(in_5), .X(X), .Y(Y), .OH(MultH), .OL(MultL));
  Div div_1 (.in_2(X), .in_3(Y), .DivR(DivRem), .Div(Div), .in_1(in_5));
  and and_2 (mult, ~in_3[0], in_3[1], ~in_3[2], ~in_3[3]);  // AND_Gate
  and and_3 (and_3_out, in_3[0], in_3[1], ~in_3[2], ~in_3[3]);  // AND_Gate
  Multiplexer #(.width(32)) multiplexer_1 (.in0(DivRem), .in1(MultH), .out(multiplexer_1_out), .sel(mult));  // open: en
  or or_2 (Enable, mult, and_3_out);
  Register #(.width(32)) register_1 (.D(multiplexer_1_out), .en(Enable), .Q(OH), .clk(in_4));  // open: clr
  Multiplexer #(.width(32)) multiplexer_2 (.in0(Div), .in1(MultL), .out(multiplexer_2_out), .sel(mult));  // open: en
  Multiplexer #(.select(4), .width(32)) multiplexer_3 (
    .in0(ADD), .in1(SUB), .in4(SLT), .in5(AND), .in6(OR), .in7(NOR), .in8(XOR), .out(OUT), .sel(in_3));  // open: in2, in3, in9, in10, in11, in12, in13, in14, in15, en
  Register #(.width(32)) register_2 (.D(multiplexer_2_out), .en(Enable), .Q(OL), .clk(in_4));  // open: clr

  // Other names for the same wires on the sheet: Clk = in_4; Select[3:0] = in_3; Sign = in_5
endmodule

// Select(ALU)
module ALUSelect (
  input  in_1,
  input  in_2,
  input  in_3,
  input  in_4,
  input  in_5,
  input  in_6,
  input  in_7,
  input  in_8,
  input  in_9,
  input  in_10,
  input  in_11,
  input  in_12,
  input  in_13,
  input  in_14,
  input  in_15,
  input  in_16,
  input  in_17,
  input  in_18,
  output I,
  output Sign,
  output [3:0] Select
);

  wire AND, DIV, MULT, OR, SLT, SLTI;

  or or_1 (Select[0], DIV, AND, in_4, in_8);
  or or_2 (I, in_17, in_14, in_12, in_6, in_3);
  or or_3 (Select[2], SLT, AND, SLTI, OR, in_8);
  or or_4 (Select[1], DIV, OR, MULT, in_8);
  or or_5 (Sign, in_13, in_7, in_15, in_17);
  or or_6 (DIV, in_13, in_16);
  or or_7 (MULT, in_7, in_10);
  or or_8 (SLT, in_15, in_18);
  or or_9 (SLTI, in_17, in_9);
  or or_10 (AND, in_2, in_12);
  or or_11 (OR, in_5, in_3);
  or or_12 (Select[3], in_11, in_6);

  // Other names for the same wires on the sheet: Add = in_1; Addi = in_14; And_t = in_2; Andi = in_12; Div_t = in_13;
  //   Divu = in_16; Mult_t = in_7; Mulu = in_10; Nor = in_8; Or_t = in_5; Ori = in_3; _0 = Select[0]; _1 = Select[1];
  //   _2 = Select[2]; _3 = Select[3]; XOR = Select[3]; Slt_t = in_15; Slti_t = in_17; Sltiu = in_9; Sltu = in_18;
  //   Sub = in_4; Xor_t = in_11; Xori = in_6
endmodule

// ID
module InstructionDecoder (
  input  [31:0] in_1,
  output [4:0] out_2,
  output out_3,
  output out_4,
  output out_5,
  output [4:0] out_6,
  output out_7,
  output out_8,
  output out_9,
  output [4:0] out_10,
  output out_11,
  output out_12,
  output out_13,
  output out_14,
  output out_15,
  output out_16,
  output [25:0] out_17,
  output out_18,
  output out_19,
  output out_20,
  output out_21,
  output out_22,
  output out_23,
  output [15:0] out_24,
  output out_25,
  output out_26,
  output out_27,
  output out_28,
  output out_29,
  output out_30,
  output out_31,
  output out_32,
  output out_33,
  output out_34,
  output out_35,
  output out_36,
  output out_37,
  output out_38,
  output out_39,
  output out_40,
  output out_41,
  output out_42
);

  wire _000000, _111111, comparator_17_eq, comparator_18_eq, comparator_19_eq, comparator_20_eq,
       comparator_21_eq, comparator_22_eq, comparator_23_eq, comparator_24_eq, comparator_25_eq,
       comparator_26_eq, comparator_27_eq, comparator_28_eq, comparator_29_eq, comparator_30_eq,
       comparator_31_eq, comparator_32_eq, comparator_33_eq, comparator_34_eq, comparator_35_eq,
       comparator_36_eq, comparator_37_eq, comparator_38_eq, comparator_39_eq, comparator_40_eq;

  Comparator #(.width(6)) comparator_1 (.a(in_1[31:26]), .b({6{1'b1}}), .eq(_111111));  // open: gt, lt
  Comparator #(.width(6)) comparator_2 (.a(in_1[31:26]), .b({6{1'b0}}), .eq(_000000));  // open: gt, lt
  Comparator #(.width(6)) comparator_3 (.a(in_1[31:26]), .b(6'b001000), .eq(out_28));  // open: gt, lt
  Comparator #(.width(6)) comparator_4 (.a(in_1[31:26]), .b(6'b001010), .eq(out_30));  // open: gt, lt
  Comparator #(.width(6)) comparator_5 (.a(in_1[31:26]), .b(6'b001011), .eq(out_32));  // open: gt, lt
  Comparator #(.width(6)) comparator_6 (.a(in_1[31:26]), .b(6'b001100), .eq(out_34));  // open: gt, lt
  Comparator #(.width(6)) comparator_7 (.a(in_1[31:26]), .b(6'b001101), .eq(out_36));  // open: gt, lt
  Comparator #(.width(6)) comparator_8 (.a(in_1[31:26]), .b(6'b001110), .eq(out_38));  // open: gt, lt
  Comparator #(.width(6)) comparator_9 (.a(in_1[31:26]), .b(6'b100011), .eq(out_5));  // open: gt, lt
  Comparator #(.width(6)) comparator_10 (.a(in_1[31:26]), .b(6'b101011), .eq(out_9));  // open: gt, lt
  Comparator #(.width(6)) comparator_11 (.a(in_1[31:26]), .b(6'b000100), .eq(out_13));  // open: gt, lt
  Comparator #(.width(6)) comparator_12 (.a(in_1[31:26]), .b(6'b000101), .eq(out_16));  // open: gt, lt
  Comparator #(.width(6)) comparator_13 (.a(in_1[31:26]), .b(6'b000110), .eq(out_19));  // open: gt, lt
  Comparator #(.width(6)) comparator_14 (.a(in_1[31:26]), .b(6'b000111), .eq(out_21));  // open: gt, lt
  Comparator #(.width(6)) comparator_15 (.a(in_1[31:26]), .b(6'b000001), .eq(out_23));  // open: gt, lt
  Comparator #(.width(6)) comparator_16 (.a(in_1[31:26]), .b(6'b000010), .eq(out_26));  // open: gt, lt
  Comparator #(.width(6)) comparator_17 (.a(in_1[5:0]), .b(6'b101011), .eq(comparator_17_eq));  // open: gt, lt
  Comparator #(.width(6)) comparator_18 (.a(in_1[5:0]), .b(6'b100100), .eq(comparator_18_eq));  // open: gt, lt
  Comparator #(.width(6)) comparator_19 (.a(in_1[5:0]), .b(6'b100101), .eq(comparator_19_eq));  // open: gt, lt
  Comparator #(.width(6)) comparator_20 (.a(in_1[5:0]), .b(6'b100111), .eq(comparator_20_eq));  // open: gt, lt
  Comparator #(.width(6)) comparator_21 (.a(in_1[5:0]), .b(6'b101000), .eq(comparator_21_eq));  // open: gt, lt
  Comparator #(.width(6)) comparator_22 (.a(in_1[5:0]), .b(6'b001000), .eq(comparator_22_eq));  // open: gt, lt
  Comparator #(.width(6)) comparator_23 (.a(in_1[5:0]), .b(6'b010000), .eq(comparator_23_eq));  // open: gt, lt
  Comparator #(.width(6)) comparator_24 (.a(in_1[5:0]), .b(6'b010010), .eq(comparator_24_eq));  // open: gt, lt
  Comparator #(.width(6)) comparator_25 (.a(in_1[5:0]), .b({6{1'b0}}), .eq(comparator_25_eq));  // open: gt, lt
  Comparator #(.width(6)) comparator_26 (.a(in_1[5:0]), .b(6'b100000), .eq(comparator_26_eq));  // open: gt, lt
  Comparator #(.width(6)) comparator_27 (.a(in_1[5:0]), .b(6'b100010), .eq(comparator_27_eq));  // open: gt, lt
  Comparator #(.width(6)) comparator_28 (.a(in_1[5:0]), .b(6'b011000), .eq(comparator_28_eq));  // open: gt, lt
  Comparator #(.width(6)) comparator_29 (.a(in_1[5:0]), .b(6'b011001), .eq(comparator_29_eq));  // open: gt, lt
  Comparator #(.width(6)) comparator_30 (.a(in_1[5:0]), .b(6'b011010), .eq(comparator_30_eq));  // open: gt, lt
  Comparator #(.width(6)) comparator_31 (.a(in_1[5:0]), .b(6'b011011), .eq(comparator_31_eq));  // open: gt, lt
  Comparator #(.width(6)) comparator_32 (.a(in_1[5:0]), .b(6'b101010), .eq(comparator_32_eq));  // open: gt, lt
  and and_1 (out_27, _000000, comparator_17_eq);
  and and_2 (out_29, _000000, comparator_18_eq);
  and and_3 (out_31, _000000, comparator_19_eq);
  and and_4 (out_33, _000000, comparator_20_eq);
  and and_5 (out_35, _000000, comparator_21_eq);
  and and_6 (out_37, _000000, comparator_22_eq);
  and and_7 (out_39, _000000, comparator_23_eq);
  and and_8 (out_41, _000000, comparator_24_eq);
  and and_9 (out_4, _000000, comparator_25_eq);
  and and_10 (out_8, _000000, comparator_26_eq);
  and and_11 (out_12, _000000, comparator_27_eq);
  and and_12 (out_15, _000000, comparator_28_eq);
  and and_13 (out_18, _000000, comparator_29_eq);
  and and_14 (out_20, _000000, comparator_30_eq);
  and and_15 (out_22, _000000, comparator_31_eq);
  and and_16 (out_25, _000000, comparator_32_eq);
  and and_17 (out_7, _111111, comparator_33_eq);
  Comparator #(.width(6)) comparator_33 (.a(in_1[5:0]), .b({6{1'b1}}), .eq(comparator_33_eq));  // open: gt, lt
  and and_18 (out_11, _111111, comparator_34_eq);
  Comparator #(.width(6)) comparator_34 (.a(in_1[5:0]), .b(6'b000001), .eq(comparator_34_eq));  // open: gt, lt
  and and_19 (out_14, _111111, comparator_35_eq);
  Comparator #(.width(6)) comparator_35 (.a(in_1[5:0]), .b(6'b000010), .eq(comparator_35_eq));  // open: gt, lt
  Comparator #(.width(6)) comparator_36 (.a(in_1[31:26]), .b(6'b111000), .eq(comparator_36_eq));  // open: gt, lt
  and and_20 (out_40, comparator_36_eq, comparator_37_eq);
  Comparator #(.width(6)) comparator_37 (.a(in_1[5:0]), .b({6{1'b0}}), .eq(comparator_37_eq));  // open: gt, lt
  Comparator #(.width(6)) comparator_38 (.a(in_1[31:26]), .b(6'b111000), .eq(comparator_38_eq));  // open: gt, lt
  and and_21 (out_42, comparator_38_eq, comparator_39_eq);
  Comparator #(.width(6)) comparator_39 (.a(in_1[5:0]), .b(6'b000001), .eq(comparator_39_eq));  // open: gt, lt
  and and_22 (out_3, _111111, comparator_40_eq);
  Comparator #(.width(6)) comparator_40 (.a(in_1[5:0]), .b(6'b000100), .eq(comparator_40_eq));  // open: gt, lt

  assign out_2 = in_1[25:21];
  assign out_6 = in_1[20:16];
  assign out_10 = in_1[15:11];
  assign out_17 = in_1[25:0];
  assign out_24 = in_1[15:0];

  // Other names for the same wires on the sheet: Add = out_8; Addi = out_28; And = out_29; Andi = out_34;
  //   Bgtz = out_21; Blez = out_19; Bltz = out_23; Bne = out_16; Bqe = out_13; Const[15:0] = in_1[15:0];
  //   Dest[25:0] = in_1[25:0]; FC[5:0] = in_1[5:0]; RD[4:0] = in_1[15:11]; RT[4:0] = in_1[20:16];
  //   RS[4:0] = in_1[25:21]; Div = out_20; Divu = out_22; Halt = out_7; J = out_26; Jr = out_37; Kbd = out_3;
  //   Lw = out_5; Mfhi = out_39; Mflo = out_41; Mult = out_15; Mulu = out_18; Nop = out_4; Nor = out_33;
  //   OP[5:0] = in_1[31:26]; Or = out_31; Ori = out_36; Pop = out_40; Push = out_42; Rnd = out_14; Slt = out_25;
  //   Slti = out_30; Sltiu = out_32; Sltu = out_27; Sub = out_12; Sw = out_9; Tty = out_11; Xor = out_35;
  //   Xori = out_38
endmodule

// DP
module DataPath (
  input  [31:0] in_1,
  input  [6:0] in_2,
  input  in_3,
  input  in_4,
  input  in_5,
  input  in_6,
  input  in_7,
  input  in_8,
  input  in_9,
  output [31:0] ROut,
  output [31:0] Address,
  output [6:0] TtyData,
  output out_13,
  output out_14,
  output out_15,
  output out_16,
  output out_17,
  output out_18,
  output out_19,
  output out_20
);

  wire Add, Addi, Addii, And, Andi, Bgtz, Blez, Bltz, Bne, Bqe, Div, Divu, I, J, Jr, Kbd, Lw, Mfhi, Mflo,
       Mult, Mulu, Nop, Nor, Or, or_7_out, or_8_out, or_9_out, Ori, Pop, Push, Rnd_t, Sign, Slt, Slti, Sltiu,
       Sltu, Sub, Sw, Xor, Xori;
  wire [3:0] AluSelect;
  wire [4:0] RD, RS, RT, Select;
  wire [15:0] Const;
  wire [25:0] Dest;
  wire [31:0] AluOut, HI, inout_1_output, Inst, LO, P, PCIn, PCOut, RND, RT_t, SP, Y;
  wire [31:7] RS_t;
  wire [31:31] and_1_out;

  BranchControl branchcontrol_1 (
    .in_1(Dest), .in_8({RS_t, TtyData}), .in_11(RT_t), .in_12(PCOut), .in_4(Const), .in_2(Bqe), .in_3(Bne),
    .in_5(Blez), .in_6(Bgtz), .in_7(Bltz), .in_9(Jr), .in_10(J), .OUT(PCIn));
  or or_1 (out_17, Rnd_t, Mfhi, Mflo, Kbd, out_14);
  or or_2 (out_19, Bgtz, Bqe, Bne, Blez, Bltz, Jr, J, Nop);
  or or_3 (out_20, Push, Sw);
  or or_4 (out_18, Push, Pop);
  or or_5 (out_16, Lw, Sw);
  ProcessInRF processinrf_1 (
    .in_4(AluOut), .in_8(RND), .in_9(in_1), .in_11(HI), .in_12(LO), .in_10(in_2), .in_1(Lw), .in_2(Pop),
    .in_3(Mfhi), .in_5(Mflo), .in_6(Kbd), .in_7(Rnd_t), .out_13(P));
  RegisterFile registerfile_1 (
    .in_10(P), .in_3(Select), .in_4(RS), .in_5(RT), .in_6(in_4), .in_7(in_7), .in_8(Push), .in_9(Pop),
    .in_1(in_3), .in_2(in_5), .SP(SP), .OX({RS_t, TtyData}), .OY(RT_t));
  Multiplexer #(.width(32)) multiplexer_1 (.in0({RS_t, TtyData}), .in1(RT_t), .out(ROut), .sel(Sw));  // open: en
  InOut inout_1 (.in_1(in_1), .Output(inout_1_output));
  Register #(.width(32)) register_1 (.D(inout_1_output), .en(in_9), .Q(Inst), .clk(in_3), .clr(in_5));
  and and_1 (and_1_out[31], ~Xori, ~Andi, ~Ori, Const[15]);  // AND_Gate
  Multiplexer #(.width(32)) multiplexer_2 (
    .in0(RT_t), .in1({{16{and_1_out[31]}}, Const}), .out(Y), .sel(I));  // open: en
  ALU alu_1 (.X({RS_t, TtyData}), .Y(Y), .in_3(AluSelect), .in_4(in_3), .in_5(Sign), .OUT(AluOut), .OH(HI), .OL(LO));
  or or_6 (Addii, Sw, Addi, Lw);
  Multiplexer #(.width(5)) multiplexer_3 (.in0(RD), .in1(RT), .out(Select), .sel(I));  // open: en
  InstructionDecoder instructiondecoder_1 (
    .out_4(Nop), .out_27(Sltu), .out_5(Lw), .out_28(Addi), .out_2(RS), .in_1(Inst), .out_8(Add),
    .out_29(And), .out_9(Sw), .out_30(Slti), .out_17(Dest), .out_6(RT), .out_12(Sub), .out_31(Or),
    .out_13(Bqe), .out_32(Sltiu), .out_10(RD), .out_15(Mult), .out_33(Nor), .out_16(Bne), .out_34(Andi),
    .out_24(Const), .out_18(Mulu), .out_35(Xor), .out_19(Blez), .out_36(Ori), .out_20(Div), .out_37(Jr),
    .out_21(Bgtz), .out_38(Xori), .out_22(Divu), .out_39(Mfhi), .out_23(Bltz), .out_25(Slt), .out_41(Mflo),
    .out_26(J), .out_40(Pop), .out_42(Push), .out_7(out_13), .out_11(out_14), .out_14(Rnd_t), .out_3(Kbd));
  Random #(.width(32)) random_1 (.clk(in_3), .next(Rnd_t), .out(RND));  // open: clr
  ProgramCounter programcounter_1 (.in_1(PCIn), .out_5(PCOut), .in_4(in_5), .in_3(in_3), .in_2(in_7));
  Adderss_Memory adderss_memory_1 (
    .in_1(PCOut), .in_2(AluOut), .in_3(SP), .in_4(Lw), .in_5(Sw), .in_6(Pop), .in_7(Push), .in_8(in_8),
    .OUT(Address));
  or or_7 (or_7_out, Xori, Mult, Nor, Mulu, Xor, Div, Addi, Divu);
  ALUSelect aluselect_1 (
    .in_1(Add), .in_2(And), .in_3(Ori), .in_4(Sub), .in_5(Or), .in_6(Xori), .in_7(Mult), .in_8(Nor),
    .in_10(Mulu), .in_11(Xor), .in_13(Div), .in_14(Addii), .in_16(Divu), .in_17(Slti), .in_15(Slt),
    .in_9(Sltiu), .in_18(Sltu), .in_12(Andi), .Sign(Sign), .Select(AluSelect), .I(I));
  or or_8 (or_8_out, Add, And, Ori, Sub, Or);
  or or_9 (or_9_out, Slti, Slt, Sltiu, Sltu, Andi);
  or or_10 (out_15, or_8_out, or_7_out, or_9_out);

  // Other names for the same wires on the sheet: AluInst = out_15; Clk = in_3; enGI = in_9; enPC = in_7; enRF = in_4;
  //   Halt = out_13; Instruction[31:0] = in_1; JmpInst = out_19; KbdAva = in_6; KbdData[6:0] = in_2; MemInst = out_16;
  //   Nextl = in_8; Reset = in_5; RInst = out_17; RS_t[6:0] = TtyData; StackInst = out_18; Tty = out_14;
  //   WriteInst = out_20
endmodule

// CU
module ControlUnit (
  input  in_1,
  input  in_2,
  input  in_3,
  input  in_4,
  input  in_5,
  input  in_6,
  input  in_7,
  input  in_8,
  input  in_9,
  input  in_10,
  input  in_11,
  input  in_12,
  output out_13,
  output out_14,
  output out_15,
  output out_16,
  output out_17,
  output out_18,
  output out_19,
  output out_20,
  output out_21
);

  wire Branch, d_ff_1_q, d_ff_2_q, d_ff_3_q, d_ff_5_q, demultiplexer_1_out0, demultiplexer_1_out1, or_5_out,
       RF;
  wire [2:0] or_1_out;

  D_Flip_Flop #(.trigger("falling")) d_ff_1 (.clk(in_1), .D(in_2), .Q(d_ff_1_q), .reset(in_6));  // open: Qn, preset, en
  or or_1 (or_1_out[0], in_5, in_4, in_11);
  or or_2 (or_1_out[1], in_5, in_9);
  or or_3 (or_1_out[2], in_10, in_11);
  D_Flip_Flop #(.trigger("falling")) d_ff_2 (.clk(in_1), .D(in_3), .Q(d_ff_2_q));  // open: Qn, preset, en, reset
  D_Flip_Flop #(.trigger("falling")) d_ff_3 (
    .clk(in_1), .D(out_14), .Q(d_ff_3_q), .reset(in_6));  // open: Qn, preset, en
  Demultiplexer #(.select(3)) demultiplexer_1 (
    .out0(demultiplexer_1_out0), .out1(demultiplexer_1_out1), .out2(Branch), .out3(RF), .out4(out_16),
    .out5(out_21), .in(d_ff_2_q), .sel(or_1_out));  // open: out6, out7, en
  or or_4 (out_17, d_ff_1_q, d_ff_3_q);
  or or_5 (or_5_out, out_15, demultiplexer_1_out0);
  D_Flip_Flop #(.trigger("falling")) d_ff_4 (
    .clk(in_1), .D(or_5_out), .Q(out_15), .reset(in_6));  // open: Qn, preset, en
  D_Flip_Flop #(.trigger("falling")) d_ff_5 (
    .clk(in_1), .D(demultiplexer_1_out1), .Q(d_ff_5_q), .reset(in_6));  // open: Qn, preset, en
  or or_6 (out_13, d_ff_5_q, in_8, RF);
  D_Flip_Flop #(.trigger("falling")) d_ff_6 (.clk(in_1), .D(out_13), .Q(out_20));  // open: Qn, preset, en, reset
  or or_7 (out_14, out_20, in_12, Branch);
  and and_1 (out_19, out_20, in_7);

  assign out_18 = in_3;

  // Other names for the same wires on the sheet: AluInst = in_4; Clk = in_1; End = out_15; getData = out_16;
  //   getInst = out_17; JmpInst = in_9; MemInst = in_10; ReadyData = in_8; ReadyW = in_12; Reset = in_6; RInst = in_5;
  //   Start = in_2; KbdEn = out_20; Tty = out_20; TtyEn = out_19; TtyInst = in_7; ReadyInst = in_3; useGI = in_3;
  //   Cont = out_14; usePC = out_14; useRF = out_13; Write = out_21; WriteInst = in_11
endmodule

// RI
module InteractuarConRam (
  input  in_1,
  input  [31:0] in_2,
  input  [31:0] in_3,
  input  in_4,
  input  in_5,
  input  in_6,
  input  [31:0] in_7,
  input  in_8,
  input  in_9,
  input  [3:0] in_10,
  input  [31:0] in_11,
  input  [3:0] in_12,
  input  [31:0] in_13,
  output out_14,
  output [31:0] out_15,
  output out_16,
  output out_17,
  output out_18,
  output [15:0] out_19,
  output out_20,
  output [31:0] out_21,
  output [3:0] out_22,
  output [31:0] out_23,
  output [31:0] out_24
);

  wire CSD, CSI, or_1_out, Stop0;
  wire [31:0] DO0, DO1, DO2, DO3, inout_1_output, inout_2_output, inout_3_output, inout_4_output, IO0, IO1,
       IO2, IO3;

  or or_1 (or_1_out, in_5, Stop0);
  D_Flip_Flop #(.trigger("falling")) d_ff_1 (
    .clk(in_1), .D(in_5), .Q(out_16), .en(or_1_out));  // open: Qn, preset, reset
  Timer timer_1 (.in_1(out_16), .in_2(out_20), .in_3(in_1), .in_4(in_10), .Ready(Stop0));
  D_Flip_Flop #(.trigger("falling")) d_ff_2 (.clk(in_1), .D(Stop0), .Q(out_20));  // open: Qn, preset, en, reset
  or or_2 (out_14, CSI, out_16, CSD);
  Demultiplexer #(.select(2)) demultiplexer_1 (
    .out0(out_22[0]), .out1(out_22[1]), .out2(out_22[2]), .out3(out_22[3]), .in(1'b1), .sel(in_3[3:2]));  // open: en
  Multiplexer #(.width(32)) multiplexer_1 (.in0(inout_1_output), .in1(IO0), .out(out_15), .sel(in_4));  // open: en
  Multiplexer #(.width(32)) multiplexer_2 (.in0(inout_2_output), .in1(IO1), .out(out_21), .sel(in_4));  // open: en
  Multiplexer #(.width(32)) multiplexer_3 (.in0(inout_3_output), .in1(IO2), .out(out_23), .sel(in_4));  // open: en
  Multiplexer #(.width(32)) multiplexer_4 (.in0(inout_4_output), .in1(IO3), .out(out_24), .sel(in_4));  // open: en
  InOut inout_1 (.in_1(DO0), .Output(inout_1_output));
  InOut inout_2 (.in_1(DO1), .Output(inout_2_output));
  InOut inout_3 (.in_1(DO2), .Output(inout_3_output));
  InOut inout_4 (.in_1(DO3), .Output(inout_4_output));
  LeerRam leerram_1 (
    .in_2(in_2), .in_3(in_7), .in_4(in_11), .in_5(in_13), .in_1(in_12), .in_6(in_1), .in_7(in_6),
    .in_8(in_9), .out_10(DO0), .out_11(DO1), .out_12(DO2), .out_13(DO3), .out_9(CSD), .out_14(out_18));
  LeerRam leerram_2 (
    .in_2(in_2), .in_3(in_7), .in_4(in_11), .in_5(in_13), .in_1(in_12), .in_6(in_1), .in_7(in_6),
    .in_8(in_8), .out_10(IO0), .out_11(IO1), .out_12(IO2), .out_13(IO3), .out_9(CSI), .out_14(out_17));

  assign out_19 = in_3[19:4];

  // Other names for the same wires on the sheet: Bank0[31:0] = in_2; Bank1[31:0] = in_7; Bank2[31:0] = in_11;
  //   Bank3[31:0] = in_13; BankOut0[31:0] = out_15; BankOut1[31:0] = out_21; BankOut2[31:0] = out_23;
  //   BankOut3[31:0] = out_24; Clk = in_1; CS = out_14; DPAddress[31:0] = in_3; ADDR[15:0] = in_3[19:4];
  //   getData = in_9; getInst = in_8; isInst = in_4; MASK[3:0] = out_22; ReadTime[3:0] = in_12; ReadyData = out_18;
  //   ReadyInst = out_17; ReadyWrite = out_20; Reset = in_6; RW = out_16; Write = in_5; WriteTime[3:0] = in_10
endmodule

module LeerRam (
  input  [3:0] in_1,
  input  [31:0] in_2,
  input  [31:0] in_3,
  input  [31:0] in_4,
  input  [31:0] in_5,
  input  in_6,
  input  in_7,
  input  in_8,
  output out_9,
  output [31:0] out_10,
  output [31:0] out_11,
  output [31:0] out_12,
  output [31:0] out_13,
  output out_14
);

  wire a, or_1_out, Stop, x;

  or or_1 (or_1_out, in_8, Stop);
  Register #(.width(32)) register_1 (.D(in_2), .en(x), .Q(out_10), .clk(in_6), .clr(in_7));
  D_Flip_Flop #(.trigger("falling")) d_ff_1 (.clk(in_6), .D(in_8), .Q(a), .en(or_1_out));  // open: Qn, preset, reset
  Timer timer_1 (.in_1(a), .in_2(out_14), .in_3(in_6), .in_4(in_1), .Ready(Stop));
  Register #(.width(32)) register_2 (.D(in_5), .en(x), .Q(out_13), .clk(in_6), .clr(in_7));
  D_Flip_Flop #(.trigger("falling")) d_ff_2 (.clk(in_6), .D(Stop), .Q(x), .reset(out_14));  // open: Qn, preset, en
  Register #(.width(32)) register_3 (.D(in_3), .en(x), .Q(out_11), .clk(in_6), .clr(in_7));
  D_Flip_Flop #(.trigger("falling")) d_ff_3 (.clk(in_6), .D(x), .Q(out_14));  // open: Qn, preset, en, reset
  or or_2 (out_9, x, a);
  Register #(.width(32)) register_4 (.D(in_4), .en(x), .Q(out_12), .clk(in_6), .clr(in_7));

  // Other names for the same wires on the sheet: Bank0[31:0] = in_2; Bank1[31:0] = in_3; Bank2[31:0] = in_4;
  //   Bank3[31:0] = in_5; BankOut0[31:0] = out_10; BankOut1[31:0] = out_11; BankOut2[31:0] = out_12;
  //   BankOut3[31:0] = out_13; Clk = in_6; CS = out_9; get = in_8; ReadTime[3:0] = in_1; Ready = out_14; Reset = in_7
endmodule

// BC
module BranchControl (
  input  [25:0] in_1,
  input  in_2,
  input  in_3,
  input  [15:0] in_4,
  input  in_5,
  input  in_6,
  input  in_7,
  input  [31:0] in_8,
  input  in_9,
  input  in_10,
  input  [31:0] in_11,
  input  [31:0] in_12,
  output [31:0] OUT
);

  wire and_1_out, and_2_out, and_3_out, and_4_out, and_5_out, comparator_1_eq, or_2_out, RS_0, RS__0, RS__RT;
  wire [1:0] or_3_out;
  wire [31:0] PC_4, PC_4_Const;
  wire [31:18] bit_extender_1_out;

  and and_1 (and_1_out, in_2, RS__RT);
  and and_2 (and_2_out, ~RS__RT, in_3);  // AND_Gate
  and and_3 (and_3_out, in_5, RS__0);
  and and_4 (and_4_out, ~RS__0, in_6);  // AND_Gate
  and and_5 (and_5_out, in_7, RS_0);
  or or_1 (RS__0, comparator_1_eq, RS_0);
  Comparator #(.width(32)) comparator_1 (.a(in_8), .b({32{1'b0}}), .eq(comparator_1_eq), .lt(RS_0));  // open: gt
  Comparator #(.width(32)) comparator_2 (.a(in_8), .b(in_11), .eq(RS__RT));  // open: gt, lt
  or or_2 (or_2_out, and_1_out, and_2_out, and_3_out, and_4_out, and_5_out);
  or or_3 (or_3_out[0], or_2_out, in_9);
  or or_4 (or_3_out[1], in_10, in_9);
  Adder #(.width(32)) adder_1 (.a(in_12), .b(32'h4), .out(PC_4));  // open: cin, cout
  Multiplexer #(.select(2), .width(32)) multiplexer_1 (
    .in0(PC_4), .in1(PC_4_Const), .in2({in_12[31:28], in_1, 2'b00}), .in3(in_8), .out(OUT), .sel(or_3_out));  // open: en
  assign bit_extender_1_out = {{13{in_4[15]}}, in_4[15]};  // Bit_Extender bit_extender_1
  Adder #(.width(32)) adder_2 (.a(PC_4), .b({bit_extender_1_out, in_4, 2'b00}), .out(PC_4_Const));  // open: cin, cout

  // Other names for the same wires on the sheet: Const[15:0] = in_4; Beq = in_2; Bgtz = in_6; Blez = in_5;
  //   Bltz = in_7; Bne = in_3; J = in_10; Dest[25:0] = in_1; Jmp[31:2] = {in_12[31:28], in_1}; PC[31:0] = in_12;
  //   Jr = in_9; RS[31:0] = in_8; RT[31:0] = in_11
endmodule

// MA
module Adderss_Memory (
  input  [31:0] in_1,
  input  [31:0] in_2,
  input  [31:0] in_3,
  input  in_4,
  input  in_5,
  input  in_6,
  input  in_7,
  input  in_8,
  output [31:0] OUT
);

  wire [1:0] or_2_out;
  wire [31:0] multiplexer_1_out, subtractor_1_out;

  Subtractor #(.width(32)) subtractor_1 (.a(in_3), .b(32'h4), .out(subtractor_1_out));  // open: bin, bout
  Multiplexer #(.width(32)) multiplexer_1 (
    .in0(in_3), .in1(subtractor_1_out), .out(multiplexer_1_out), .sel(in_7));  // open: en
  Multiplexer #(.select(2), .width(32)) multiplexer_2 (
    .in0(in_1), .in1(in_2), .in2(multiplexer_1_out), .in3(in_1), .out(OUT), .sel(or_2_out));  // open: en
  or or_1 (or_2_out[1], in_6, in_8, in_7);
  or or_2 (or_2_out[0], in_4, in_8, in_5);

  // Other names for the same wires on the sheet: ALU[31:0] = in_2; isPC = in_8; Lw = in_4; PC[31:0] = in_1;
  //   Pop = in_6; Push = in_7; SP[31:0] = in_3; Sw = in_5
endmodule

// PC
module ProgramCounter (
  input  [31:0] in_1,
  input  in_2,
  input  in_3,
  input  in_4,
  output [31:0] out_5
);

  Register #(.width(32)) register_1 (.D(in_1), .en(in_2), .Q(out_5), .clk(in_3), .clr(in_4));

  // Other names for the same wires on the sheet: Imput[31:0] = in_1; Out[31:0] = out_5
endmodule

// Multip
module Multi (
  input  in_1,
  input  [31:0] X,
  input  [31:0] Y,
  output [31:0] OH,
  output [31:0] OL
);

  wire and_1_out, Overflow, Overflow1, shr_2_out_4, shr_4_out_4, SigX, SigY;
  wire [31:0] NA, NAA, NB, NBB, OH1, OH2, OL1, OL2, RH, RH1, RL, RL1, shl_1_x_2, shl_2_x_2, shr_1_x_2,
       shr_6_x_2, shr_7_x_2, subtractor_1_out, SumX, SumY;

  and and_1 (and_1_out, SigX, SigY);
  SHR shr_1 (.X({32{1'b0}}), .in_1(and_1_out), .X_2(shr_1_x_2));  // open: out_4
  Subtractor #(.width(32)) subtractor_1 (.a(X), .b(shr_1_x_2), .out(subtractor_1_out));  // open: bin, bout
  SHL shl_1 (.X(X), .in_2(1'b0), .out_3(SigX), .X_2(shl_1_x_2));
  SHL shl_2 (.X(Y), .in_2(1'b0), .out_3(SigY), .X_2(shl_2_x_2));
  Multiplexer #(.width(32)) multiplexer_1 (
    .in0({32{1'b0}}), .in1(subtractor_1_out), .out(SumX), .sel(SigY));  // open: en
  Multiplexer #(.width(32)) multiplexer_2 (.in0({32{1'b0}}), .in1(Y), .out(SumY), .sel(SigX));  // open: en
  Multiplier #(.width(32)) multiplier_1 (.a(X), .b(Y), .out(OL1), .cout(OH1));  // open: cin
  Multiplier #(.width(32)) multiplier_2 (.a(shl_1_x_2), .b(shl_2_x_2), .out(OL2), .cout(OH2));  // open: cin
  SHR shr_2 (.X(OL2), .in_1(1'b0), .out_4(shr_2_out_4), .X_2(NA));
  SHR shr_3 (.X(OH2), .in_1(shr_2_out_4), .X_2(NB));  // open: out_4
  SHR shr_4 (.X(NA), .in_1(1'b0), .out_4(shr_4_out_4), .X_2(NAA));
  SHR shr_5 (.X(NB), .in_1(shr_4_out_4), .X_2(NBB));  // open: out_4
  Adder #(.width(32)) adder_1 (.a(NAA), .b(SumX), .out(RL), .cout(Overflow));  // open: cin
  Adder #(.width(32)) adder_2 (.a(RL), .b(SumY), .out(RL1), .cout(Overflow1));  // open: cin
  SHR shr_6 (.X({32{1'b0}}), .in_1(Overflow), .X_2(shr_6_x_2));  // open: out_4
  SHR shr_7 (.X({32{1'b0}}), .in_1(Overflow1), .X_2(shr_7_x_2));  // open: out_4
  Multiplexer #(.width(32)) multiplexer_3 (.in0(RL1), .in1(OL1), .out(OL), .sel(in_1));  // open: en
  Multiplexer #(.width(32)) multiplexer_4 (.in0(RH1), .in1(OH1), .out(OH), .sel(in_1));  // open: en
  Adder #(.width(32)) adder_3 (.a(NBB), .b(shr_6_x_2), .out(RH));  // open: cin, cout
  Adder #(.width(32)) adder_4 (.a(RH), .b(shr_7_x_2), .out(RH1));  // open: cin, cout

  // Other names for the same wires on the sheet: Sign = in_1
endmodule

// Divi
module Div (
  input  in_1,
  input  [31:0] in_2,
  input  [31:0] in_3,
  output [31:0] DivR,
  output [31:0] Div
);

  wire shr_1_out_4, shr_2_out_4, SignoA, SignoB, xor_1_out;
  wire [31:0] A1, adder_1_out, B1, Div_t, multiplexer_1_out, negator_1_out, negator_2_out, negator_3_out, R,
       subtractor_1_out;

  SHR shr_1 (.X(in_2), .in_1(1'b0), .out_4(shr_1_out_4));  // open: X_2
  SHR shr_2 (.X(in_3), .in_1(1'b0), .out_4(shr_2_out_4));  // open: X_2
  and and_1 (SignoA, in_1, shr_1_out_4);
  and and_2 (SignoB, in_1, shr_2_out_4);
  Multiplexer #(.width(32)) multiplexer_1 (
    .in0(Div_t), .in1(adder_1_out), .out(multiplexer_1_out), .sel(SignoA));  // open: en
  Adder #(.width(32)) adder_1 (.a(Div_t), .b(32'h1), .out(adder_1_out));  // open: cin, cout
  Negator #(.width(32)) negator_1 (.in(in_2), .out(negator_1_out));
  Negator #(.width(32)) negator_2 (.in(in_3), .out(negator_2_out));
  Multiplexer #(.width(32)) multiplexer_2 (.in0(in_2), .in1(negator_1_out), .out(A1), .sel(SignoA));  // open: en
  Multiplexer #(.width(32)) multiplexer_3 (.in0(in_3), .in1(negator_2_out), .out(B1), .sel(SignoB));  // open: en
  Multiplexer #(.width(32)) multiplexer_4 (
    .in0(multiplexer_1_out), .in1(negator_3_out), .out(Div), .sel(xor_1_out));  // open: en
  Negator #(.width(32)) negator_3 (.in(multiplexer_1_out), .out(negator_3_out));
  xor xor_1 (xor_1_out, SignoB, SignoA);
  Divider #(.width(32)) divider_1 (.a(A1), .b(B1), .out(Div_t), .rem(R));  // open: upper
  Subtractor #(.width(32)) subtractor_1 (.a(B1), .b(R), .out(subtractor_1_out));  // open: bin, bout
  Multiplexer #(.width(32)) multiplexer_5 (.in0(R), .in1(subtractor_1_out), .out(DivR), .sel(SignoA));  // open: en

  // Other names for the same wires on the sheet: A[31:0] = in_2; B[31:0] = in_3; OH[31:0] = DivR; OL[31:0] = Div;
  //   Signo = in_1
endmodule

module Comp (
  input  [31:0] in_1,
  input  [31:0] in_2,
  input  in_3,
  output Comp
);

  wire and_1_out, and_2_out, comparator_1_lt, comparator_2_lt;

  Comparator #(.width(32)) comparator_1 (.a(in_1), .b(in_2), .lt(comparator_1_lt));  // open: gt, eq
  Comparator #(.width(32), .mode("unsigned")) comparator_2 (.a(in_1), .b(in_2), .lt(comparator_2_lt));  // open: gt, eq
  and and_1 (and_1_out, comparator_1_lt, in_3);
  and and_2 (and_2_out, ~in_3, comparator_2_lt);  // AND_Gate
  or or_1 (Comp, and_1_out, and_2_out);

  // Other names for the same wires on the sheet: A[31:0] = in_1; B[31:0] = in_2; Signo = in_3
endmodule

module SHL (
  input  [31:0] X,
  input  in_2,
  output out_3,
  output [31:0] X_2
);


  assign out_3 = X[0];
  assign X_2 = {in_2, X[31:1]};
endmodule

module SHR (
  input  in_1,
  input  [31:0] X,
  output [31:0] X_2,
  output out_4
);


  assign out_4 = X[31];
  assign X_2 = {X[30:0], in_1};
endmodule

// IO
module InOut (
  input  [31:0] in_1,
  output [31:0] Output
);


  assign Output = {in_1[7:0], in_1[15:8], in_1[23:16], in_1[31:24]};
endmodule

module Timer (
  input  in_1,
  input  in_2,
  input  in_3,
  input  [3:0] in_4,
  output Ready
);

  wire [3:0] counter_1_q;

  Counter #(.width(4), .max('hf)) counter_1 (
    .count(in_1), .Q(counter_1_q), .clk(in_3), .clr(in_2));  // open: load, D, carry
  Comparator #(.width(4)) comparator_1 (.a(in_4), .b(counter_1_q), .eq(Ready));  // open: gt, lt

  // Other names for the same wires on the sheet: Clk = in_3; Reset = in_2; Start = in_1; Time[3:0] = in_4
endmodule
